# Fritzing sketch DHT11_Schematic (saved by Fritzing 1.0.2b)
breadboards: 1

parts:
  Part1 = Arduino Uno (Rev3)
  Part2 = LCD1602-I2C
  RHT1 = Humidity and Temperature Sensor RHT03

nets:
  N1: Part1.A0, Part2.SCL
  N2: Part1.A1, Part2.SDA
  N3: Part1.D2, RHT1.Data-signal
  N4: Part1.GND, RHT1.GND_2

custom parts:
  LCD1602-I2C: A standard character display, usually with 2x16 characters. Comes in many colors with LCM1602 IIC attached.
