# Fritzing sketch DHT11_Schematic_esp8266 (saved by Fritzing 1.0.2b)
breadboards: 1

parts:
  Part2 = LCD1602-I2C
  RHT1 = Humidity and Temperature Sensor RHT03
  Mod1 = Amica NodeMCU DEVKIT 1.0

nets:
  N1: Part2.GND, RHT1.GND_2
  N2: Part2.SDA, Mod1.pin_13
  N3: Part2.SCL, Mod1.pin_14
  N4: RHT1.Vcc, Mod1.pin_30
  N5: RHT1.Data-signal, Mod1.pin_12

custom parts:
  LCD1602-I2C: A standard character display, usually with 2x16 characters. Comes in many colors with LCM1602 IIC attached.
